// Logisim project 4-1-bit-full-Adder.circ as structural Verilog: 5 circuits, main circuit main
module main (
  input  Cin,
  input  A0,
  input  B0,
  input  A1,
  input  B1,
  input  A2,
  input  B2,
  input  A3,
  input  B3,
  output S0,
  output S1,
  output S2,
  output S3,
  output Cout
);

  wire adder_1_cout, adder_2_cout, adder_3_cout;

  Adder #(.width(1)) adder_1 (.a(A0), .b(B0), .out(S0), .cin(Cin), .cout(adder_1_cout));
  Adder #(.width(1)) adder_2 (.a(A1), .b(B1), .out(S1), .cin(adder_1_cout), .cout(adder_2_cout));
  Adder #(.width(1)) adder_3 (.a(A2), .b(B2), .out(S2), .cin(adder_2_cout), .cout(adder_3_cout));
  Adder #(.width(1)) adder_4 (.a(A3), .b(B3), .out(S3), .cin(adder_3_cout), .cout(Cout));
endmodule

module Xor (
  input  x,
  input  Y,
  input  Z,
  output S,
  output C
);

  wire and_1_out, X___Y_out, XY_out;

  xor X___Y (X___Y_out, x, Y);
  and and_1 (and_1_out, X___Y_out, Z);
  and XY (XY_out, x, Y);
  xor xor_1 (S, X___Y_out, Z);
  or or_1 (C, and_1_out, XY_out);
endmodule

module _2_2_bit_full_adder (
  input  Cin,
  input  A0,
  input  B0,
  input  A1,
  input  B1,
  output S0,
  output S1,
  output Cout
);

  wire adder_1_cout;

  Adder #(.width(1)) adder_1 (.a(A0), .b(B0), .out(S0), .cin(Cin), .cout(adder_1_cout));
  Adder #(.width(1)) adder_2 (.a(A1), .b(B1), .out(S1), .cin(adder_1_cout), .cout(Cout));
endmodule

module Use_4_bit_adder (
  input  Cin,
  input  A0,
  input  B0,
  input  A1,
  input  B1,
  input  A2,
  input  B2,
  input  A3,
  input  B3,
  output S0,
  output S1,
  output S2,
  output S3,
  output Cout
);

  main main_1 (
    .Cin(Cin), .A0(A0), .B0(B0), .A1(A1), .B1(B1), .A2(A2), .B2(B2), .A3(A3), .B3(B3), .S0(S0), .S1(S1),
    .S2(S2), .S3(S3), .Cout(Cout));
endmodule

module USE_2_BIT_ADDER (
  input  Cin,
  input  A0,
  input  B0,
  input  A1,
  input  B1,
  input  A2,
  input  B2,
  input  A3,
  input  B3,
  output S0,
  output S1,
  output S3,
  output S4,
  output Cout
);

  wire n2_2_bit_full_adder_1_cout;

  _2_2_bit_full_adder u_2_2_bit_full_adder_1 (
    .Cin(Cin), .A0(A0), .B0(B0), .A1(A1), .B1(B1), .S0(S0), .S1(S1), .Cout(n2_2_bit_full_adder_1_cout));
  _2_2_bit_full_adder u_2_2_bit_full_adder_2 (
    .Cin(n2_2_bit_full_adder_1_cout), .A0(A2), .B0(B2), .A1(A3), .B1(B3), .S0(S3), .S1(S4), .Cout(Cout));
endmodule
