// Logisim project Decoder.circ as structural Verilog: 1 circuit, main circuit main
module main (
  input  A2,
  input  A1,
  input  A0
);

  wire decoder_4_out0, decoder_4_out2, not_1_out, undriven;
  wire [1:0] undriven_2;

  not not_1 (not_1_out, A2);
  Decoder decoder_1 (.sel(A1), .en(not_1_out));  // open: out0, out1
  Decoder decoder_2 (.sel(A0), .en(A2));  // open: out0, out1
  Decoder #(.select(2)) decoder_3 ();  // open: out0, out1, out2, out3, sel, en
  Decoder #(.select(2)) decoder_4 (
    .out0(decoder_4_out0), .out1(decoder_4_out0), .out2(decoder_4_out2), .out3(decoder_4_out0),
    .sel(undriven_2), .en(undriven));
endmodule
