// Logisim project 2to4BitDecoder.circ as structural Verilog: 1 circuit, main circuit main
module main (
  input  E,
  input  in_2,
  input  in_3,
  output out_4,
  output out_5,
  output out_6,
  output out_7
);

  // _74139 74139_1: pin names not known; wires that end beside it: E, in_2, in_3, out_4, out_5, out_6, out_7, 1'b0, 1'b1
endmodule
