// Logisim project 3To8BitDecoderUsing2To4.circ as structural Verilog: 1 circuit, main circuit main
module main (
  input  E,
  input  B,
  input  A,
  output out_4,
  output out_5,
  output out_6,
  output out_7,
  output out_8,
  output out_9,
  output out_10,
  output out_11
);

  wire main_1_out_4, main_1_out_5, main_1_out_6, main_1_out_7, main_2_out_4, main_2_out_5, main_2_out_6,
       main_2_out_7, n7404_1_p2;

  // _7404 7404_1: pin names not known; wires that end beside it: E, n7404_1_p2, 1'b0, 1'b1
  _2to4BitDecoder_main main_1 (
    .E(E), .in_2(B), .in_3(A), .out_4(main_1_out_4), .out_5(main_1_out_5), .out_6(main_1_out_6),
    .out_7(main_1_out_7));
  _2to4BitDecoder_main main_2 (
    .E(n7404_1_p2), .in_2(B), .in_3(A), .out_4(main_2_out_4), .out_5(main_2_out_5), .out_6(main_2_out_6),
    .out_7(main_2_out_7));
  // _7432 7432_1: pin names not known; wires that end beside it: main_1_out_4, E, out_4, E, main_1_out_5, out_5, 1'b0, 1'b1, E, main_1_out_6, out_6, E, main_1_out_7, out_7
  // _7432 7432_2: pin names not known; wires that end beside it: main_2_out_4, n7404_1_p2, out_8, main_2_out_5, n7404_1_p2, out_9, 1'b0, 1'b1, main_2_out_6, n7404_1_p2, out_10, main_2_out_7, n7404_1_p2, out_11
endmodule
