// Logisim project Full_adder.circ as structural Verilog: 2 circuits, main circuit main
module main (
  input  X,
  input  Y,
  input  Z
);

  wire n7408_1_pin3, n7408_1_pin11, n7432_1_p4, n7486_1_pin8, n7486_1_pin11;

  _7486 u_7486_1 (
    .pin13(Y), .pin12(X), .pin11(n7486_1_pin11), .pin10(n7486_1_pin11), .pin9(Z), .pin8(n7486_1_pin8));  // open: pin1, pin2, pin3, pin4, pin5, pin6
  _7408 u_7408_1 (
    .pin1(Y), .pin2(X), .pin3(n7408_1_pin3), .pin13(n7486_1_pin11), .pin12(Z), .pin11(n7408_1_pin11));  // open: pin4, pin5, pin6, pin10, pin9, pin8
  // Probe on n7486_1_pin8
  // Probe on n7432_1_p4
  // _7432 7432_1: pin names not known; wires that end beside it: 1'b1, n7408_1_pin3, n7408_1_pin11, n7432_1_p4, 1'b0
endmodule

module two_bit_adder (
  input  in_1,
  input  in_2,
  input  in_3,
  input  in_4,
  input  in_5
);

  wire undriven, undriven_2, undriven_3, undriven_4;

  main main_1 (.X(undriven_4), .Y(undriven_2), .Z(in_1));
  main main_2 (.X(undriven_3), .Y(undriven), .Z(in_4));
  // Probe on undriven_3
  // Probe on undriven_2
  // Probe on undriven
endmodule
