// Logisim project lab2_report.circ as structural Verilog: 1 circuit, main circuit main
module main (
  input  X,
  input  Y,
  input  Z,
  input  X1,
  input  Y1,
  input  Z1
);

  wire and_1_out, and_2_out, and_3_out, and_4_out, not_1_out, not_2_out, or_1_out, or_2_out, or_3_out,
       or_4_out, or_5_out, undriven;

  not not_1 (not_1_out, undriven);
  not not_2 (not_2_out, X1);
  or or_1 (or_1_out, X1, Y1);
  or or_2 (or_2_out, X, Y);
  or or_3 (or_3_out, not_1_out, Z);
  or or_4 (or_4_out, Y, Z);
  and and_1 (and_1_out, or_1_out, Z1);
  and and_2 (and_2_out, or_2_out, or_3_out);
  and and_3 (and_3_out, not_2_out, Y1);
  and and_4 (and_4_out, and_2_out, or_4_out);
  LED led_1 (.in(and_4_out));
  or or_5 (or_5_out, and_3_out, and_1_out);
  LED led_2 (.in(or_5_out));

  // Notes on the sheet:
  //   x
endmodule
