// Logisim project two_bit_adder.circ as structural Verilog: 2 circuits, main circuit main
module main (
  input  A,
  input  B,
  input  Cin,
  output Sum,
  output Cout
);

  wire n7408_1_p3, n7408_1_p6, n7486_1_p4;

  // _7486 7486_1: pin names not known; wires that end beside it: Sum, A, B, n7486_1_p4, n7486_1_p4, Cin, Sum, 1'b0, 1'b1
  // _7408 7408_1: pin names not known; wires that end beside it: B, A, n7408_1_p3, n7486_1_p4, Cin, n7408_1_p6, 1'b0, 1'b1
  // _7432 7432_1: pin names not known; wires that end beside it: n7408_1_p3, n7408_1_p6, Cout, 1'b0, 1'b1, 1'b1, 1'b0
endmodule

module two_bit_adder (
  input  A0,
  input  B0,
  input  Cin,
  input  A1,
  input  B1,
  output S0,
  output S1_prime,
  output Cout
);

  wire main_1_cout;

  main main_1 (.A(A0), .B(B0), .Cin(Cin), .Sum(S0), .Cout(main_1_cout));
  main main_2 (.A(A1), .B(B1), .Cin(main_1_cout), .Sum(S1_prime), .Cout(Cout));

  // Notes on the sheet:
  //   2
  //   1
  //   4
endmodule
